// Digital circuit part_c.dig as structural Verilog
module part_c (
  input  in_0,
  input  in_1,
  input  in_2,
  output out_0
);

  wire nfet_3_s, nfet_6_d, nfet_7_s, nfet_14_s, pfet_1_d, pfet_2_d, pfet_3_d, pfet_5_d, pfet_6_d, pfet_8_d,
       pfet_9_d, pfet_10_d, pfet_12_d, pfet_13_d, pfet_16_d;

  PFET pfet_1 (.G(in_0), .S(1'b1), .D(pfet_1_d));
  NFET nfet_1 (.G(in_0), .D(pfet_1_d), .S(1'b0));
  PFET pfet_2 (.G(in_2), .S(1'b1), .D(pfet_2_d));
  NFET nfet_2 (.G(in_2), .D(pfet_2_d), .S(1'b0));
  PFET pfet_3 (.G(pfet_1_d), .S(1'b1), .D(pfet_3_d));
  NFET nfet_3 (.G(pfet_1_d), .D(pfet_3_d), .S(nfet_3_s));
  NFET nfet_4 (.G(pfet_2_d), .D(nfet_3_s), .S(1'b0));
  PFET pfet_4 (.G(pfet_2_d), .S(1'b1), .D(pfet_3_d));
  PFET pfet_5 (.G(pfet_3_d), .S(1'b1), .D(pfet_5_d));
  NFET nfet_5 (.G(pfet_3_d), .D(pfet_5_d), .S(1'b0));
  NFET nfet_6 (.G(pfet_16_d), .D(nfet_6_d), .S(1'b0));
  PFET pfet_6 (.G(in_0), .S(1'b1), .D(pfet_6_d));
  NFET nfet_7 (.G(in_0), .D(pfet_6_d), .S(nfet_7_s));
  NFET nfet_8 (.G(in_2), .D(nfet_7_s), .S(1'b0));
  NFET nfet_9 (.G(pfet_8_d), .D(nfet_6_d), .S(1'b0));
  PFET pfet_7 (.G(in_2), .S(1'b1), .D(pfet_6_d));
  NFET nfet_10 (.G(pfet_5_d), .D(nfet_6_d), .S(1'b0));
  PFET pfet_8 (.G(pfet_6_d), .S(1'b1), .D(pfet_8_d));
  NFET nfet_11 (.G(pfet_6_d), .D(pfet_8_d), .S(1'b0));
  PFET pfet_9 (.G(pfet_5_d), .S(1'b1), .D(pfet_9_d));
  PFET pfet_10 (.G(pfet_8_d), .S(pfet_9_d), .D(pfet_10_d));
  PFET pfet_11 (.G(pfet_16_d), .S(pfet_10_d), .D(nfet_6_d));
  PFET pfet_12 (.G(in_1), .S(1'b1), .D(pfet_12_d));
  NFET nfet_12 (.G(in_1), .D(pfet_12_d), .S(1'b0));
  PFET pfet_13 (.G(in_0), .S(1'b1), .D(pfet_13_d));
  PFET pfet_14 (.G(nfet_6_d), .S(1'b1), .D(out_0));
  NFET nfet_13 (.G(nfet_6_d), .D(out_0), .S(1'b0));
  PFET pfet_15 (.G(pfet_12_d), .S(1'b1), .D(pfet_13_d));
  NFET nfet_14 (.G(in_0), .D(pfet_13_d), .S(nfet_14_s));
  NFET nfet_15 (.G(pfet_12_d), .D(nfet_14_s), .S(1'b0));
  PFET pfet_16 (.G(pfet_13_d), .S(1'b1), .D(pfet_16_d));
  NFET nfet_16 (.G(pfet_13_d), .D(pfet_16_d), .S(1'b0));
endmodule

/* Test case part_c_test:
in_0 in_1 in_2 out_0
0    0    0    1
0    0    1    0
0    1    0    1
0    1    1    0
1    0    0    1
1    0    1    1
1    1    0    0
1    1    1    1
*/
